# Fritzing sketch Inscryption (saved by Fritzing 0.9.3b)
breadboards: 1

parts:
  Part1 = Arduino Uno (Rev3)
  C1 = Electrolytic Capacitor [capacitance=100µF voltage=50V package="100 mil [THT, electrolytic]"]
  R1 = Resistor [tolerance=±10% resistance=2k package=THT]
  R2 = Resistor [tolerance=±10% resistance=2k package=THT]
  R3 = Resistor [tolerance=±10% resistance=2k package=THT]
  Part2 = I2C level shifter bidirectional
  Part3 = I2C level shifter bidirectional
  Part4 = I2C level shifter bidirectional
  Part5 = I2C level shifter bidirectional
  Part6 = RFID-RC522-v2
  Part7 = RFID-RC522-v2
  Part8 = RFID-RC522-v2
  Part9 = RFID-RC522-v2
  Part10 = RFID-RC522-v2
  Part11 = RFID-RC522-v2
  Part12 = RFID-RC522-v2
  Part13 = RFID-RC522-v2
  Part14 = RFID-RC522-v2
  Part15 = RFID-RC522-v2
  Mod1 = KY-032 IR Obstacle Avoidance Sensor Module [package="Breakout board"]
  Mod2 = KY-032 IR Obstacle Avoidance Sensor Module [package="Breakout board"]
  Mod4 = KY-032 IR Obstacle Avoidance Sensor Module [package="Breakout board"]
  Mod5 = KY-032 IR Obstacle Avoidance Sensor Module [package="Breakout board"]
  Mod6 = KY-032 IR Obstacle Avoidance Sensor Module [package="Breakout board"]
  Mod7 = KY-032 IR Obstacle Avoidance Sensor Module [package="Breakout board"]
  Mod8 = KY-032 IR Obstacle Avoidance Sensor Module [package="Breakout board"]
  Mod9 = KY-032 IR Obstacle Avoidance Sensor Module [package="Breakout board"]
  Mod10 = KY-032 IR Obstacle Avoidance Sensor Module [package="Breakout board"]
  Mod11 = KY-032 IR Obstacle Avoidance Sensor Module [package="Breakout board"]
  U2 = 74HC165 [part_number=SN74LS165 package="DIP16 [THT]"]  # not connected
  U3 = 74HC165 [part_number=SN74LS165 package="DIP16 [THT]"]
  R4 = Resistor [tolerance=±5% resistance=10k package=THT]
  R5 = Resistor [tolerance=±5% resistance=10k package=THT]
  R6 = Resistor [tolerance=±5% resistance=10k package=THT]
  R7 = Resistor [tolerance=±5% resistance=10k package=THT]
  R10 = Resistor [tolerance=±5% resistance=10k package=THT]
  R11 = Resistor [tolerance=±5% resistance=10k package=THT]
  R12 = Resistor [tolerance=±5% resistance=10k package=THT]
  R13 = Resistor [tolerance=±5% resistance=10k package=THT]
  R14 = Resistor [tolerance=±5% resistance=10k package=THT]
  R15 = Resistor [tolerance=±5% resistance=10k package=THT]
  MUX1 = 74HC4051 [package="DIP (Dual Inline) [THT]"]  # not connected

nets:
  N1: Part1.A0, R3.Pin_1
  N2: Part1.A1, R2.Pin_1
  N3: Part1.A2, R1.Pin_1
  N4: Part1.A3, U3.Q1
  N5: Part1.D9_PWM, Part5.HV1
  N6: Part1.D11_PWM/MOSI, Part5.HV3
  N7: Part1.D12/MISO, Part5.HV2
  N8: Part1.D13/SCK, Part5.HV4
  N9: Part1.D2, Part4.HV2
  N10: Part1.D3_PWM, Part4.HV1
  N11: Part1.D6_PWM, U3.Q2
  3.3V: Part1.3V3, Part2.LV, Part3.LV, Part4.LV, Part5.LV, Part6.3.3V, Part7.3.3V, Part8.3.3V, Part9.3.3V, Part10.3.3V, Part11.3.3V, Part12.3.3V, Part13.3.3V, Part14.3.3V, Part15.3.3V
  5V: Part1.5V, C1.+, Part2.HV, Part3.HV, Part4.HV, Part5.HV, Mod1.+, Mod2.+, Mod4.+, Mod5.+, Mod6.+, Mod7.+, Mod8.+, Mod9.+, Mod10.+, Mod11.+, U3.Q3, U3.Q4, U3.Q5, U3.Q6, U3.OE, U3.DS, U3.VCC
  GND: Part1.GND, C1.-, Part2.GND, Part3.GND, Part4.GND, Part5.GND, Part6.GND, Part7.GND, Part8.GND, Part9.GND, Part10.GND, Part11.GND, Part12.GND, Part13.GND, Part14.GND, Part15.GND, Mod1.GND, Mod2.GND, Mod4.GND, Mod5.GND, Mod6.GND, Mod7.GND, Mod8.GND, Mod9.GND, Mod10.GND, Mod11.GND, U3.GND
  N12: Part2.LV4, Part8.SDA
  N13: Part2.LV3, Part7.SDA
  N14: Part2.LV2, Part6.SDA
  N15: Part2.LV1, Part14.SDA
  N16: Part3.LV4, Part12.SDA
  N17: Part3.LV3, Part11.SDA
  N18: Part3.LV2, Part10.SDA
  N19: Part3.LV1, Part9.SDA
  N20: Part4.LV2, Part13.SDA
  N21: Part4.LV1, Part15.SDA
  N22: Part5.LV4, Part6.SCK, Part7.SCK, Part8.SCK, Part9.SCK, Part10.SCK, Part11.SCK, Part12.SCK, Part13.SCK, Part14.SCK, Part15.SCK
  N23: Part5.LV3, Part6.MOSI, Part7.MOSI, Part8.MOSI, Part9.MOSI, Part10.MOSI, Part11.MOSI, Part12.MOSI, Part13.MOSI, Part14.MOSI, Part15.MOSI
  N24: Part5.LV2, Part6.MISO, Part7.MISO, Part8.MISO, Part9.MISO, Part10.MISO, Part11.MISO, Part12.MISO, Part13.MISO, Part14.MISO, Part15.MISO
  N25: Part5.LV1, Part6.RST, Part7.RST, Part8.RST, Part9.RST, Part10.RST, Part11.RST, Part12.RST, Part13.RST, Part14.RST, Part15.RST
  N26: Mod1.out, R11.Pin_0
  N27: Mod2.out, R7.Pin_0
  N28: Mod4.out, R14.Pin_0
  N29: Mod5.out, R15.Pin_0
  N30: Mod6.out, R4.Pin_0
  N31: Mod7.out, R5.Pin_0
  N32: Mod8.out, R6.Pin_0
  N33: Mod9.out, R10.Pin_0
  N34: Mod10.out, R13.Pin_0
  N35: Mod11.out, R12.Pin_0
  N36: U3.SH_CP, R15.Pin_1
  N37: U3.ST_CP, R14.Pin_1

custom parts:
  RFID-RC522-v2: A simple China made RFID-RC522 Reader; do check the pin labels, as this is a MFRC522 based clone.
  KY-032 IR Obstacle Avoidance Sensor Module: KY-032 Infrared Obstacle Avoidance Sensor. Distance-adjustable, infrared proximity sensor designed for wheeled robots. Also known as AD-032.
  74HC165: 8-bit parallel-load shift registers
  74HC4051: 8 channel analog multiplexer/demultiplexer
